// Logisim project ALU_Group07.circ as structural Verilog: 15 circuits, main circuit main
module main (
  output halt,
  output [8:0] counter,
  output [3:0] op,
  output [11:0] a,
  output [11:0] b,
  output [11:0] oracle,
  output [11:0] result,
  output err_oracle,
  output error,
  output ok,
  output start_delimiter
);

  wire and_1_out, and_2_out, clock_1_out, comparator_1_eq, comparator_2_eq;

  Clock clock_1 (.out(clock_1_out));
  Counter #(.width(9), .max('h1ff), .trigger("falling")) counter_1 (
    .Q(counter), .carry(halt), .clk(clock_1_out));  // open: load, D, count, clr
  RAM #(.addrWidth(12), .dataWidth(4), .bus("separate")) ram_1 (
    .addr({counter, 3'b000}), .data(op), .ld(1'b1));  // open: din, str, sel, clk, clr
  RAM #(.addrWidth(12), .dataWidth(12), .bus("separate")) ram_2 (
    .addr({counter, 3'b001}), .data(a), .ld(1'b1));  // open: din, str, sel, clk, clr
  RAM #(.addrWidth(12), .dataWidth(12), .bus("separate")) ram_3 (
    .addr({counter, 3'b010}), .data(b), .ld(1'b1));  // open: din, str, sel, clk, clr
  RAM #(.addrWidth(12), .dataWidth(12), .bus("separate")) ram_4 (
    .addr({counter, 3'b011}), .data(oracle), .ld(1'b1));  // open: din, str, sel, clk, clr
  RAM #(.addrWidth(12), .dataWidth(1), .bus("separate")) ram_5 (
    .addr({counter, 3'b100}), .data(err_oracle), .ld(1'b1));  // open: din, str, sel, clk, clr
  RAM #(.addrWidth(12), .dataWidth(1), .bus("separate")) ram_6 (
    .addr({counter, 3'b101}), .data(start_delimiter), .ld(1'b1));  // open: din, str, sel, clk, clr
  _12_bit_ALU u_12_bit_alu_1 (.ALU_code(op), .a(a), .b(b), .overflow(error), .result(result));
  Comparator #(.width(1), .mode("unsigned")) comparator_1 (
    .a(error), .b(err_oracle), .eq(comparator_1_eq));  // open: gt, lt
  Comparator #(.width(12)) comparator_2 (.a(result), .b(oracle), .eq(comparator_2_eq));  // open: gt, lt
  and and_1 (and_1_out, comparator_1_eq, error);
  and and_2 (and_2_out, comparator_2_eq, comparator_1_eq, ~error);  // AND_Gate
  or or_1 (ok, and_1_out, and_2_out);

  // Notes on the sheet:
  //   You must complete the circuit '12-bit ALU' instead.
  //   DO NOT EDIT THIS CIRCUIT!
endmodule

module _12_bit_ALU (
  input  [3:0] ALU_code,
  input  [11:0] a,
  input  [11:0] b,
  output [11:0] result,
  output overflow
);

  wire Add_overflow, Inverse_out_3, Shift_left_arithmetic_out_3, Subtract_out_4;
  wire [11:0] Add_out_4, and_1_out, Equals_out_3, Generate_0_out_1, Greater_than_out_3, Inverse_out_2,
       Less_than_out_3, Not_equals_out_3, Not_out, or_1_out, Shift_left_arithmetic_out_2,
       Shift_left_logical_out_2, Shift_right_arithmetic_out_2, Shift_right_logical_out_2, Subtract_out_3;

  _12bit_CLA Add (.in_1(b), .in_2(a), .in_3(1'b0), .out_4(Add_out_4), .Overflow(Add_overflow));
  generate_0 Generate_0 (.out_1(Generate_0_out_1));
  assign and_1_out = a & b;  // AND_Gate and_1, 12 bits wide
  assign or_1_out = b | a;  // OR_Gate or_1, 12 bits wide
  _12_bit_numeric_subtraction Subtract (.in_1(a), .in_2(b), .out_3(Subtract_out_3), .out_4(Subtract_out_4));
  less_than Less_than (.in_1(a), .out_3(Less_than_out_3), .in_2(b));
  greater_than Greater_than (.in_1(a), .in_2(b), .out_3(Greater_than_out_3));
  equals Equals (.in_1(a), .in_2(b), .out_3(Equals_out_3));
  not_equals Not_equals (.in_1(a), .in_2(b), .out_3(Not_equals_out_3));
  assign Not_out = ~a;  // NOT_Gate Not, 12 bits wide
  inverse Inverse (.in_1(a), .out_2(Inverse_out_2), .out_3(Inverse_out_3));
  shift_left_logical Shift_left_logical (.in_1(a), .out_2(Shift_left_logical_out_2));
  shift_right_logical Shift_right_logical (.in_1(a), .out_2(Shift_right_logical_out_2));
  shift_left_arithmetic Shift_left_arithmetic (
    .in_1(a), .out_2(Shift_left_arithmetic_out_2), .out_3(Shift_left_arithmetic_out_3));
  shift_right_arithmetic Shift_right_arithmetic (.in_1(a), .out_2(Shift_right_arithmetic_out_2));
  Multiplexer #(.select(4), .width(12)) multiplexer_1 (
    .in0(Generate_0_out_1), .in1(and_1_out), .in2(or_1_out), .in3(Add_out_4), .in4(Subtract_out_3),
    .in5(Less_than_out_3), .in6(Greater_than_out_3), .in7(Equals_out_3), .in8(Not_equals_out_3),
    .in9(Not_out), .in10(Inverse_out_2), .in11(Shift_left_logical_out_2), .in12(Shift_right_logical_out_2),
    .in13(Shift_left_arithmetic_out_2), .in14(Shift_right_arithmetic_out_2), .in15(a), .out(result),
    .sel(ALU_code));  // open: en
  Multiplexer #(.select(4)) multiplexer_2 (
    .in0(1'b0), .in1(1'b0), .in2(1'b0), .in3(Add_overflow), .in4(Subtract_out_4), .in5(1'b0), .in6(1'b0),
    .in7(1'b0), .in8(1'b0), .in9(1'b0), .in10(Inverse_out_3), .in11(1'b0), .in12(1'b0),
    .in13(Shift_left_arithmetic_out_3), .in14(1'b0), .in15(1'b0), .out(overflow), .sel(ALU_code));  // open: en

  // Notes on the sheet:
  //   Do not change the circuit appearance.
  //   DO NOT CHANGE THE INPUTS AND OUTPUTS OF THIS CIRCUIT!
  //   Do not add/remove inputs or outputs. Do not even change their location or orientation.
  //   And
  //   Or
endmodule

module generate_0 (
  output [11:0] out_1
);

  assign out_1 = {{11{1'b0}}, 1'b0};  // Bit_Extender bit_extender_1
endmodule

module _12_bit_numeric_subtraction (
  input  [11:0] in_1,
  input  [11:0] in_2,
  output [11:0] out_3,
  output out_4
);

  wire [11:0] not_1_out;

  assign not_1_out = ~in_2;  // NOT_Gate not_1, 12 bits wide
  _12bit_CLA u_12bit_cla_1 (.in_1(in_1), .in_2(not_1_out), .in_3(1'b1), .out_4(out_3), .Overflow(out_4));
endmodule

module less_than (
  input  [11:0] in_1,
  input  [11:0] in_2,
  output [11:0] out_3
);

  wire and_1_out, and_2_out, n12bit_cla_1_overflow, or_1_out;
  wire [11:0] n12bit_cla_1_out_4, not_1_out;

  assign not_1_out = ~in_2;  // NOT_Gate not_1, 12 bits wide
  _12bit_CLA u_12bit_cla_1 (
    .in_1(in_1), .in_2(not_1_out), .in_3(1'b1), .out_4(n12bit_cla_1_out_4), .Overflow(n12bit_cla_1_overflow));
  and and_1 (and_1_out, n12bit_cla_1_out_4[11], ~n12bit_cla_1_overflow);  // AND_Gate
  and and_2 (and_2_out, n12bit_cla_1_overflow, in_1[11]);
  or or_1 (or_1_out, and_1_out, and_2_out);
  assign out_3 = {{11{1'b0}}, or_1_out};  // Bit_Extender bit_extender_1
endmodule

module greater_than (
  input  [11:0] in_1,
  input  [11:0] in_2,
  output [11:0] out_3
);

  wire nor_1_out;
  wire [11:0] equals_1_out_3, less_than_1_out_3;

  equals equals_1 (.in_1(in_1), .in_2(in_2), .out_3(equals_1_out_3));
  less_than less_than_1 (.in_1(in_1), .out_3(less_than_1_out_3), .in_2(in_2));
  nor nor_1 (nor_1_out, less_than_1_out_3[0], equals_1_out_3[0]);
  assign out_3 = {{11{1'b0}}, nor_1_out};  // Bit_Extender bit_extender_1
endmodule

module equals (
  input  [11:0] in_1,
  input  [11:0] in_2,
  output [11:0] out_3
);

  wire and_1_out, xnor_1_out, xnor_2_out, xnor_3_out, xnor_4_out, xnor_5_out, xnor_6_out, xnor_7_out,
       xnor_8_out, xnor_9_out, xnor_10_out, xnor_11_out, xnor_12_out;

  xnor xnor_1 (xnor_1_out, in_1[0], in_2[0]);
  xnor xnor_2 (xnor_2_out, in_1[1], in_2[1]);
  xnor xnor_3 (xnor_3_out, in_1[2], in_2[2]);
  xnor xnor_4 (xnor_4_out, in_1[3], in_2[3]);
  xnor xnor_5 (xnor_5_out, in_1[4], in_2[4]);
  xnor xnor_6 (xnor_6_out, in_1[5], in_2[5]);
  xnor xnor_7 (xnor_7_out, in_1[6], in_2[6]);
  xnor xnor_8 (xnor_8_out, in_1[7], in_2[7]);
  xnor xnor_9 (xnor_9_out, in_1[8], in_2[8]);
  xnor xnor_10 (xnor_10_out, in_1[9], in_2[9]);
  xnor xnor_11 (xnor_11_out, in_1[10], in_2[10]);
  xnor xnor_12 (xnor_12_out, in_1[11], in_2[11]);
  and and_1 (and_1_out, xnor_1_out, xnor_2_out, xnor_3_out, xnor_4_out, xnor_5_out, xnor_6_out, xnor_7_out, xnor_8_out, xnor_9_out, xnor_10_out, xnor_11_out, xnor_12_out);
  assign out_3 = {{11{1'b0}}, and_1_out};  // Bit_Extender bit_extender_1
endmodule

module not_equals (
  input  [11:0] in_1,
  input  [11:0] in_2,
  output [11:0] out_3
);

  wire and_1_out, not_1_out, xnor_1_out, xnor_2_out, xnor_3_out, xnor_4_out, xnor_5_out, xnor_6_out,
       xnor_7_out, xnor_8_out, xnor_9_out, xnor_10_out, xnor_11_out, xnor_12_out;

  xnor xnor_1 (xnor_1_out, in_1[0], in_2[0]);
  xnor xnor_2 (xnor_2_out, in_1[1], in_2[1]);
  xnor xnor_3 (xnor_3_out, in_1[2], in_2[2]);
  xnor xnor_4 (xnor_4_out, in_1[3], in_2[3]);
  xnor xnor_5 (xnor_5_out, in_1[4], in_2[4]);
  xnor xnor_6 (xnor_6_out, in_1[5], in_2[5]);
  xnor xnor_7 (xnor_7_out, in_1[6], in_2[6]);
  xnor xnor_8 (xnor_8_out, in_1[7], in_2[7]);
  xnor xnor_9 (xnor_9_out, in_1[8], in_2[8]);
  xnor xnor_10 (xnor_10_out, in_1[9], in_2[9]);
  xnor xnor_11 (xnor_11_out, in_1[10], in_2[10]);
  xnor xnor_12 (xnor_12_out, in_1[11], in_2[11]);
  and and_1 (and_1_out, xnor_1_out, xnor_2_out, xnor_3_out, xnor_4_out, xnor_5_out, xnor_6_out, xnor_7_out, xnor_8_out, xnor_9_out, xnor_10_out, xnor_11_out, xnor_12_out);
  not not_1 (not_1_out, and_1_out);
  assign out_3 = {{11{1'b0}}, not_1_out};  // Bit_Extender bit_extender_1
endmodule

module inverse (
  input  [11:0] in_1,
  output [11:0] out_2,
  output out_3
);

  wire [11:0] not_1_out;

  assign not_1_out = ~in_1;  // NOT_Gate not_1, 12 bits wide
  _12bit_CLA u_12bit_cla_1 (.in_1(not_1_out), .in_2(12'h1), .in_3(1'b0), .out_4(out_2), .Overflow(out_3));
endmodule

module shift_left_logical (
  input  [11:0] in_1,
  output [11:0] out_2
);


  assign out_2 = {in_1[10:0], 1'b0};
endmodule

module shift_right_logical (
  input  [11:0] in_1,
  output [11:0] out_2
);


  assign out_2 = {1'b0, in_1[11:1]};
endmodule

module shift_left_arithmetic (
  input  [11:0] in_1,
  output [11:0] out_2,
  output out_3
);


  assign out_2 = {in_1[11], in_1[9:0], 1'b0};
  assign out_3 = in_1[10];
endmodule

module shift_right_arithmetic (
  input  [11:0] in_1,
  output [11:0] out_2
);


  assign out_2 = {in_1[11:10], in_1[10:1]};
endmodule

module _12_bit_AND (
  input  [11:0] in_1,
  input  [11:0] in_2,
  output [11:0] out_3
);

  and and_1 (out_3[0], in_1[0], in_2[0]);
  and and_2 (out_3[2], in_1[2], in_2[2]);
  and and_3 (out_3[1], in_1[1], in_2[1]);
  and and_4 (out_3[3], in_1[3], in_2[3]);
  and and_5 (out_3[4], in_1[4], in_2[4]);
  and and_6 (out_3[5], in_1[5], in_2[5]);
  and and_7 (out_3[6], in_1[6], in_2[6]);
  and and_8 (out_3[8], in_1[8], in_2[8]);
  and and_9 (out_3[7], in_1[7], in_2[7]);
  and and_10 (out_3[9], in_1[9], in_2[9]);
  and and_11 (out_3[10], in_1[10], in_2[10]);
  and and_12 (out_3[11], in_1[11], in_2[11]);
endmodule

module _12_bit_OR (
  input  [11:0] in_1,
  input  [11:0] in_2,
  output [11:0] out_3
);

  and and_1 (out_3[0], in_1[0], in_2[0]);
  and and_2 (out_3[2], in_1[2], in_2[2]);
  and and_3 (out_3[1], in_1[1], in_2[1]);
  and and_4 (out_3[4], in_1[4], in_2[4]);
  and and_5 (out_3[3], in_1[3], in_2[3]);
  and and_6 (out_3[6], in_1[6], in_2[6]);
  and and_7 (out_3[5], in_1[5], in_2[5]);
  and and_8 (out_3[8], in_1[8], in_2[8]);
  and and_9 (out_3[7], in_1[7], in_2[7]);
  and and_10 (out_3[9], in_1[9], in_2[9]);
  and and_11 (out_3[10], in_1[10], in_2[10]);
  and and_12 (out_3[11], in_1[11], in_2[11]);
endmodule
