// Logisim project csa-project-adders.circ as structural Verilog: 12 circuits, main circuit main
module main (
  input  Carry_in,
  input  A,
  input  B,
  output Carry_out,
  output Sum
);

  wire and_1_out, and_2_out, and_3_out, and_4_out, and_5_out, and_6_out, and_7_out, not_1_out, not_2_out,
       not_3_out, not_4_out, not_5_out, not_6_out;

  not not_1 (not_1_out, B);
  not not_2 (not_2_out, Carry_in);
  not not_3 (not_3_out, A);
  not not_4 (not_4_out, Carry_in);
  not not_5 (not_5_out, A);
  not not_6 (not_6_out, B);
  and and_1 (and_1_out, A, Carry_in);
  and and_2 (and_2_out, B, Carry_in);
  and and_3 (and_3_out, A, B);
  and and_4 (and_4_out, A, not_1_out, not_2_out);
  and and_5 (and_5_out, not_3_out, B, not_4_out);
  and and_6 (and_6_out, not_5_out, not_6_out, Carry_in);
  and and_7 (and_7_out, A, B, Carry_in);
  or or_1 (Carry_out, and_1_out, and_2_out, and_3_out);
  or or_2 (Sum, and_4_out, and_5_out, and_6_out, and_7_out);
endmodule

module _1bit_adder (
  input  Carry_in,
  input  A,
  input  B,
  output Carry_out,
  output Sum
);

  wire and_1_out, and_2_out, and_3_out, and_4_out, and_5_out, and_6_out, and_7_out, not_1_out, not_2_out,
       not_3_out, not_4_out, not_5_out, not_6_out;

  not not_1 (not_1_out, B);
  not not_2 (not_2_out, Carry_in);
  not not_3 (not_3_out, A);
  not not_4 (not_4_out, Carry_in);
  not not_5 (not_5_out, A);
  not not_6 (not_6_out, B);
  and and_1 (and_1_out, A, Carry_in);
  and and_2 (and_2_out, B, Carry_in);
  and and_3 (and_3_out, A, B);
  and and_4 (and_4_out, A, not_1_out, not_2_out);
  and and_5 (and_5_out, not_3_out, B, not_4_out);
  and and_6 (and_6_out, not_5_out, not_6_out, Carry_in);
  and and_7 (and_7_out, A, B, Carry_in);
  or or_1 (Carry_out, and_1_out, and_2_out, and_3_out);
  or or_2 (Sum, and_4_out, and_5_out, and_6_out, and_7_out);
endmodule

module c1 (
  input  a0,
  input  b0,
  input  Carry_in,
  output Carry_out,
  output out_5,
  output out_6
);

  wire and_2_out;

  and and_1 (out_5, b0, a0);
  or or_1 (out_6, b0, a0);
  or or_2 (Carry_out, and_2_out, out_5);
  and and_2 (and_2_out, out_6, Carry_in);

  // Notes on the sheet:
  //   g0
  //   p0
endmodule

module c2 (
  input  a0,
  input  b0,
  input  a1,
  input  b1,
  input  Carry_in,
  output out_6,
  output out_7,
  output out_8
);

  wire and_1_out, and_3_out, and_4_out, or_1_out;

  and and_1 (and_1_out, b0, a0);
  or or_1 (or_1_out, b0, a0);
  and and_2 (out_7, b1, a1);
  or or_2 (out_8, b1, a1);
  or or_3 (out_6, and_4_out, and_3_out, out_7);
  and and_3 (and_3_out, out_8, or_1_out, Carry_in);
  and and_4 (and_4_out, out_8, and_1_out);

  // Notes on the sheet:
  //   g0
  //   g1
  //   p0
  //   p1
endmodule

module c3 (
  input  a0,
  input  b0,
  input  a1,
  input  b1,
  input  a2,
  input  b2,
  input  c0,
  output out_8,
  output out_9,
  output out_10
);

  wire and_1_out, and_2_out, and_4_out, and_5_out, and_6_out, or_1_out, or_2_out;

  and and_1 (and_1_out, b0, a0);
  or or_1 (or_1_out, b0, a0);
  and and_2 (and_2_out, b1, a1);
  or or_2 (or_2_out, b1, a1);
  and and_3 (out_9, b2, a2);
  or or_3 (out_10, b2, a2);
  and and_4 (and_4_out, out_10, and_2_out);
  or or_4 (out_8, and_4_out, and_6_out, and_5_out, out_9);
  and and_5 (and_5_out, out_10, or_2_out, or_1_out, c0);
  and and_6 (and_6_out, out_10, or_2_out, and_1_out);

  // Notes on the sheet:
  //   g0
  //   p0
  //   g1
  //   p1
  //   g2
  //   p2
endmodule

module c4 (
  input  a0,
  input  b0,
  input  a1,
  input  b1,
  input  a2,
  input  b2,
  input  a2_2,
  input  b2_2,
  input  c0,
  output out_10,
  output g3,
  output p3
);

  wire and_1_out, and_2_out, and_3_out, and_5_out, and_6_out, and_7_out, and_8_out, or_1_out, or_2_out,
       or_3_out;

  and and_1 (and_1_out, b0, a0);
  or or_1 (or_1_out, b0, a0);
  and and_2 (and_2_out, b1, a1);
  or or_2 (or_2_out, b1, a1);
  and and_3 (and_3_out, b2, a2);
  or or_3 (or_3_out, b2, a2);
  and and_4 (g3, b2_2, a2_2);
  or or_4 (p3, b2_2, a2_2);
  and and_5 (and_5_out, p3, and_3_out);
  or or_5 (out_10, and_5_out, and_6_out, and_7_out, and_8_out, g3);
  and and_6 (and_6_out, p3, or_3_out, and_2_out);
  and and_7 (and_7_out, p3, or_3_out, or_2_out, and_1_out);
  and and_8 (and_8_out, p3, or_3_out, or_2_out, or_1_out, c0);

  // Notes on the sheet:
  //   g0
  //   p0
  //   g1
  //   p1
  //   g2
  //   p2
  //   g3
  //   p3
endmodule

module _4bit_CLU (
  input  a0,
  input  a1,
  input  a2,
  input  a3,
  input  b0,
  input  b1,
  input  b2,
  input  b3,
  input  c0,
  output p3,
  output g3,
  output p2,
  output g2,
  output p1,
  output g1,
  output p0,
  output g0,
  output c4,
  output c3,
  output c2,
  output c1
);

  c1 c1_1 (.a0(a0), .b0(b0), .Carry_in(c0), .Carry_out(c1), .out_5(g0), .out_6(p0));
  c2 c2_1 (.out_6(c2), .a0(a0), .b0(b0), .a1(a1), .b1(b1), .Carry_in(c0), .out_7(g1), .out_8(p1));
  c3 c3_1 (.a0(a0), .b0(b0), .a1(a1), .b1(b1), .a2(a2), .b2(b2), .c0(c0), .out_8(c3), .out_9(g2), .out_10(p2));
  c4 c4_1 (
    .a0(a0), .b0(b0), .a1(a1), .b1(b1), .a2(a2), .b2(b2), .a2_2(a3), .b2_2(b3), .c0(c0), .out_10(c4),
    .g3(g3), .p3(p3));
endmodule

module _4bit_CLA (
  input  in_1,
  input  [3:0] in_2,
  input  [3:0] in_3,
  output [3:0] out_4,
  output out_5
);

  wire and_1_out, and_2_out, and_3_out, and_4_out, and_5_out, and_6_out, and_7_out, and_8_out, and_9_out,
       and_10_out, g0_out, g1_out, g2_out, or_2_out, or_3_out, or_4_out, p0_out, p1_out, p2_out, p3_out;

  or or_1 (out_5, and_7_out, and_8_out, and_9_out, and_10_out);
  or or_2 (or_2_out, and_1_out, g0_out);
  or or_3 (or_3_out, g1_out, and_2_out, and_3_out);
  or or_4 (or_4_out, and_4_out, and_5_out, and_6_out);
  and and_1 (and_1_out, in_1, p0_out);
  and and_2 (and_2_out, g0_out, p1_out);
  and and_3 (and_3_out, in_1, p0_out, p1_out);
  and and_4 (and_4_out, g1_out, p2_out);
  and and_5 (and_5_out, g0_out, p1_out, p2_out);
  and and_6 (and_6_out, in_1, p0_out, p1_out, p2_out, p3_out);
  and and_7 (and_7_out, g2_out, p3_out);
  and and_8 (and_8_out, p3_out, p2_out, g1_out);
  and and_9 (and_9_out, g0_out, p1_out, p2_out, p3_out);
  and and_10 (and_10_out, in_1, p1_out, p2_out, p3_out, p0_out);
  _1bit_adder u_1bit_adder_1 (.A(in_2[3]), .B(in_3[3]), .Sum(out_4[3]), .Carry_in(or_4_out));  // open: Carry_out
  _1bit_adder u_1bit_adder_2 (.A(in_2[2]), .B(in_3[2]), .Sum(out_4[2]), .Carry_in(or_3_out));  // open: Carry_out
  _1bit_adder u_1bit_adder_3 (.A(in_2[1]), .B(in_3[1]), .Sum(out_4[1]), .Carry_in(or_2_out));  // open: Carry_out
  _1bit_adder u_1bit_adder_4 (.A(in_2[0]), .B(in_3[0]), .Sum(out_4[0]), .Carry_in(in_1));  // open: Carry_out
  and g0 (g0_out, in_2[0], in_3[0]);
  and g1 (g1_out, in_2[1], in_3[1]);
  and g2 (g2_out, in_2[2], in_3[2]);
  and g3 (g2_out, in_2[3], in_3[3]);
  or p0 (p0_out, in_2[0], in_3[0]);
  or p1 (p1_out, in_2[1], in_3[1]);
  or p2 (p2_out, in_2[2], in_3[2]);
  or p3 (p3_out, in_2[3], in_3[3]);

  // Notes on the sheet:
  //   c1
  //   c2
  //   c3
  //   lorem ipsum
endmodule

module _4bit_CLA__simplified (
  input  in_1,
  input  [3:0] in_2,
  input  [3:0] in_3,
  output P0,
  output G0,
  output Overflow,
  output [3:0] out_7
);

  wire and_2_out, and_3_out, and_4_out, n4bit_clu_1_c1, n4bit_clu_1_c2, n4bit_clu_1_c3, n4bit_clu_1_g0,
       n4bit_clu_1_g1, n4bit_clu_1_g2, n4bit_clu_1_g3, n4bit_clu_1_p0, n4bit_clu_1_p1, n4bit_clu_1_p2,
       n4bit_clu_1_p3;

  and and_1 (P0, n4bit_clu_1_p0, n4bit_clu_1_p1, n4bit_clu_1_p2, n4bit_clu_1_p3);
  or or_1 (G0, and_3_out, and_2_out, and_4_out, n4bit_clu_1_g3);
  and and_2 (and_2_out, n4bit_clu_1_g1, n4bit_clu_1_p2, n4bit_clu_1_p3);
  and and_3 (and_3_out, n4bit_clu_1_g0, n4bit_clu_1_p1, n4bit_clu_1_p2, n4bit_clu_1_p3);
  and and_4 (and_4_out, n4bit_clu_1_g2, n4bit_clu_1_p3);
  _1bit_adder u_1bit_adder_1 (.A(in_2[3]), .B(in_3[3]), .Sum(out_7[3]), .Carry_in(n4bit_clu_1_c3));  // open: Carry_out
  _1bit_adder u_1bit_adder_2 (.A(in_2[2]), .B(in_3[2]), .Sum(out_7[2]), .Carry_in(n4bit_clu_1_c2));  // open: Carry_out
  _1bit_adder u_1bit_adder_3 (.A(in_2[1]), .B(in_3[1]), .Sum(out_7[1]), .Carry_in(n4bit_clu_1_c1));  // open: Carry_out
  _1bit_adder u_1bit_adder_4 (.A(in_2[0]), .B(in_3[0]), .Sum(out_7[0]), .Carry_in(in_1));  // open: Carry_out
  _4bit_CLU u_4bit_clu_1 (
    .p3(n4bit_clu_1_p3), .g3(n4bit_clu_1_g3), .p2(n4bit_clu_1_p2), .g2(n4bit_clu_1_g2), .p1(n4bit_clu_1_p1),
    .g1(n4bit_clu_1_g1), .p0(n4bit_clu_1_p0), .g0(n4bit_clu_1_g0), .c4(Overflow), .c3(n4bit_clu_1_c3),
    .c2(n4bit_clu_1_c2), .c1(n4bit_clu_1_c1), .a0(in_3[0]), .a1(in_3[1]), .a2(in_3[2]), .a3(in_3[3]),
    .b0(in_2[0]), .b1(in_2[1]), .b2(in_2[2]), .b3(in_2[3]), .c0(in_1));

  // Notes on the sheet:
  //   lorem ipsum
endmodule

module _12bit_RCA (
  input  [11:0] in_1,
  input  [11:0] in_2,
  input  in_3,
  output OVERFLOW,
  output [11:0] out_5
);

  wire and_1_out, and_2_out, n1bit_adder_1_carry_out, n1bit_adder_2_carry_out, n1bit_adder_3_carry_out,
       n1bit_adder_4_carry_out, n1bit_adder_5_carry_out, n1bit_adder_6_carry_out, n1bit_adder_7_carry_out,
       n1bit_adder_8_carry_out, n1bit_adder_9_carry_out, n1bit_adder_10_carry_out, n1bit_adder_11_carry_out,
       not_1_out, not_2_out, not_3_out;

  _1bit_adder u_1bit_adder_1 (
    .A(in_1[0]), .B(in_2[0]), .Carry_out(n1bit_adder_1_carry_out), .Sum(out_5[0]), .Carry_in(in_3));
  _1bit_adder u_1bit_adder_2 (
    .A(in_1[1]), .B(in_2[1]), .Carry_out(n1bit_adder_2_carry_out), .Sum(out_5[1]),
    .Carry_in(n1bit_adder_1_carry_out));
  _1bit_adder u_1bit_adder_3 (
    .A(in_1[2]), .B(in_2[2]), .Carry_out(n1bit_adder_3_carry_out), .Sum(out_5[2]),
    .Carry_in(n1bit_adder_2_carry_out));
  _1bit_adder u_1bit_adder_4 (
    .A(in_1[3]), .B(in_2[3]), .Carry_out(n1bit_adder_4_carry_out), .Sum(out_5[3]),
    .Carry_in(n1bit_adder_3_carry_out));
  _1bit_adder u_1bit_adder_5 (
    .A(in_1[4]), .B(in_2[4]), .Carry_out(n1bit_adder_5_carry_out), .Sum(out_5[4]),
    .Carry_in(n1bit_adder_4_carry_out));
  _1bit_adder u_1bit_adder_6 (
    .A(in_1[5]), .B(in_2[5]), .Carry_out(n1bit_adder_6_carry_out), .Sum(out_5[5]),
    .Carry_in(n1bit_adder_5_carry_out));
  _1bit_adder u_1bit_adder_7 (
    .A(in_1[6]), .B(in_2[6]), .Carry_out(n1bit_adder_7_carry_out), .Sum(out_5[6]),
    .Carry_in(n1bit_adder_6_carry_out));
  _1bit_adder u_1bit_adder_8 (
    .A(in_1[7]), .B(in_2[7]), .Carry_out(n1bit_adder_8_carry_out), .Sum(out_5[7]),
    .Carry_in(n1bit_adder_7_carry_out));
  _1bit_adder u_1bit_adder_9 (
    .A(in_1[8]), .B(in_2[8]), .Carry_out(n1bit_adder_9_carry_out), .Sum(out_5[8]),
    .Carry_in(n1bit_adder_8_carry_out));
  _1bit_adder u_1bit_adder_10 (
    .A(in_1[9]), .B(in_2[9]), .Carry_out(n1bit_adder_10_carry_out), .Sum(out_5[9]),
    .Carry_in(n1bit_adder_9_carry_out));
  _1bit_adder u_1bit_adder_11 (
    .A(in_1[10]), .B(in_2[10]), .Carry_out(n1bit_adder_11_carry_out), .Sum(out_5[10]),
    .Carry_in(n1bit_adder_10_carry_out));
  _1bit_adder u_1bit_adder_12 (
    .A(in_1[11]), .B(in_2[11]), .Sum(out_5[11]), .Carry_in(n1bit_adder_11_carry_out));  // open: Carry_out
  not not_1 (not_1_out, in_2[11]);
  not not_2 (not_2_out, in_1[11]);
  and and_1 (and_1_out, not_1_out, not_2_out, out_5[11]);
  and and_2 (and_2_out, in_2[11], in_1[11], not_3_out);
  not not_3 (not_3_out, out_5[11]);
  or or_1 (OVERFLOW, and_1_out, and_2_out);
endmodule

module _12bit_CLA (
  input  [11:0] in_1,
  input  [11:0] in_2,
  input  in_3,
  output [11:0] out_4,
  output Overflow
);

  wire and_1_out, and_2_out, n4bit_cla_simplified_1_g0, n4bit_cla_simplified_1_p0, n4bit_cla_simplified_2_g0,
       n4bit_cla_simplified_2_p0, n4bit_cla_simplified_3_g0, n4bit_cla_simplified_3_p0, n12bit_clu_1_c1,
       n12bit_clu_1_c2, not_1_out, not_2_out, not_3_out;

  _4bit_CLA__simplified u_4bit_cla_simplified_1 (
    .in_2(in_2[3:0]), .in_3(in_1[3:0]), .in_1(in_3), .out_7(out_4[3:0]), .G0(n4bit_cla_simplified_1_g0),
    .P0(n4bit_cla_simplified_1_p0));  // open: Overflow
  _12bit_CLU u_12bit_clu_1 (
    .C1(n12bit_clu_1_c1), .C2(n12bit_clu_1_c2), .c0(in_3), .G0(n4bit_cla_simplified_1_g0),
    .P0(n4bit_cla_simplified_1_p0), .G1(n4bit_cla_simplified_2_g0), .P1(n4bit_cla_simplified_2_p0),
    .G2(n4bit_cla_simplified_3_g0), .P2(n4bit_cla_simplified_3_p0));  // open: C3
  not not_1 (not_1_out, in_1[11]);
  and and_1 (and_1_out, not_1_out, not_2_out, out_4[11]);
  not not_2 (not_2_out, in_2[11]);
  and and_2 (and_2_out, in_1[11], in_2[11], not_3_out);
  not not_3 (not_3_out, out_4[11]);
  or or_1 (Overflow, and_1_out, and_2_out);
  _4bit_CLA__simplified u_4bit_cla_simplified_2 (
    .in_2(in_2[7:4]), .in_3(in_1[7:4]), .in_1(n12bit_clu_1_c1), .out_7(out_4[7:4]),
    .G0(n4bit_cla_simplified_2_g0), .P0(n4bit_cla_simplified_2_p0));  // open: Overflow
  _4bit_CLA__simplified u_4bit_cla_simplified_3 (
    .in_2(in_2[11:8]), .in_3(in_1[11:8]), .in_1(n12bit_clu_1_c2), .out_7(out_4[11:8]),
    .G0(n4bit_cla_simplified_3_g0), .P0(n4bit_cla_simplified_3_p0));  // open: Overflow
endmodule

module _12bit_CLU (
  input  c0,
  input  G0,
  input  P0,
  input  G1,
  input  P1,
  input  G2,
  input  P2,
  output C1,
  output C2,
  output C3
);

  wire and_1_out, and_2_out, and_3_out, and_4_out, and_5_out, and_6_out;

  and and_1 (and_1_out, P0, c0);
  and and_2 (and_2_out, P1, G0);
  and and_3 (and_3_out, P1, P0, c0);
  and and_4 (and_4_out, P2, G1);
  and and_5 (and_5_out, P2, P1, G0);
  and and_6 (and_6_out, P2, P1, P0, c0);
  or or_1 (C1, and_1_out, G0);
  or or_2 (C2, and_2_out, and_3_out, G1);
  or or_3 (C3, and_4_out, and_5_out, and_6_out, G2);
endmodule
