// Logisim project memory.circ as structural Verilog
module _12bit_register (
  input  [11:0] Input,
  input  Reset,
  input  Write,
  input  Clock,
  output [11:0] out_5
);

  wire or_1_out;
  wire [11:0] multiplexer_1_out;

  Multiplexer #(.width(12), .enable("false")) multiplexer_1 (
    .in0(Input), .in1({12{1'b0}}), .out(multiplexer_1_out), .sel(Reset));
  or or_1 (or_1_out, Reset, Write);
  D_Flip_Flop #(.trigger("falling")) d_ff_1 (
    .clk(Clock), .D(multiplexer_1_out[5]), .Q(out_5[5]), .en(or_1_out));  // open: Qn, preset, reset
  D_Flip_Flop #(.trigger("falling")) d_ff_2 (
    .clk(Clock), .D(multiplexer_1_out[11]), .Q(out_5[11]), .en(or_1_out));  // open: Qn, preset, reset
  D_Flip_Flop #(.trigger("falling")) d_ff_3 (
    .clk(Clock), .D(multiplexer_1_out[4]), .Q(out_5[4]), .en(or_1_out));  // open: Qn, preset, reset
  D_Flip_Flop #(.trigger("falling")) d_ff_4 (
    .clk(Clock), .D(multiplexer_1_out[10]), .Q(out_5[10]), .en(or_1_out));  // open: Qn, preset, reset
  D_Flip_Flop #(.trigger("falling")) d_ff_5 (
    .clk(Clock), .D(multiplexer_1_out[3]), .Q(out_5[3]), .en(or_1_out));  // open: Qn, preset, reset
  D_Flip_Flop #(.trigger("falling")) d_ff_6 (
    .clk(Clock), .D(multiplexer_1_out[9]), .Q(out_5[9]), .en(or_1_out));  // open: Qn, preset, reset
  D_Flip_Flop #(.trigger("falling")) d_ff_7 (
    .clk(Clock), .D(multiplexer_1_out[2]), .Q(out_5[2]), .en(or_1_out));  // open: Qn, preset, reset
  D_Flip_Flop #(.trigger("falling")) d_ff_8 (
    .clk(Clock), .D(multiplexer_1_out[8]), .Q(out_5[8]), .en(or_1_out));  // open: Qn, preset, reset
  D_Flip_Flop #(.trigger("falling")) d_ff_9 (
    .clk(Clock), .D(multiplexer_1_out[1]), .Q(out_5[1]), .en(or_1_out));  // open: Qn, preset, reset
  D_Flip_Flop #(.trigger("falling")) d_ff_10 (
    .clk(Clock), .D(multiplexer_1_out[7]), .Q(out_5[7]), .en(or_1_out));  // open: Qn, preset, reset
  D_Flip_Flop #(.trigger("falling")) d_ff_11 (
    .clk(Clock), .D(multiplexer_1_out[0]), .Q(out_5[0]), .en(or_1_out));  // open: Qn, preset, reset
  D_Flip_Flop #(.trigger("falling")) d_ff_12 (
    .clk(Clock), .D(multiplexer_1_out[6]), .Q(out_5[6]), .en(or_1_out));  // open: Qn, preset, reset
endmodule

module register_file (
  input  [2:0] rs,
  input  [2:0] rt,
  input  [2:0] rd,
  input  [11:0] data,
  input  write,
  input  clock,
  input  reset,
  output [11:0] S,
  output [11:0] T
);

  wire and_1_out, and_2_out, and_3_out, and_4_out, and_5_out, and_6_out, and_7_out, and_8_out,
       decoder_1_out0, decoder_1_out1, decoder_1_out2, decoder_1_out3, decoder_1_out4, decoder_1_out5,
       decoder_1_out6, decoder_1_out7;
  wire [11:0] n12bit_register_1_out_5, n12bit_register_2_out_5, n12bit_register_3_out_5,
       n12bit_register_4_out_5, n12bit_register_5_out_5, n12bit_register_6_out_5, n12bit_register_7_out_5,
       n12bit_register_8_out_5;

  Decoder #(.select(3), .enable("false")) decoder_1 (
    .out0(decoder_1_out0), .out1(decoder_1_out1), .out2(decoder_1_out2), .out3(decoder_1_out3),
    .out4(decoder_1_out4), .out5(decoder_1_out5), .out6(decoder_1_out6), .out7(decoder_1_out7), .sel(rd));
  and and_1 (and_1_out, write, decoder_1_out0);
  and and_2 (and_2_out, write, decoder_1_out1);
  and and_3 (and_3_out, write, decoder_1_out2);
  and and_4 (and_4_out, write, decoder_1_out3);
  and and_5 (and_5_out, write, decoder_1_out4);
  and and_6 (and_6_out, write, decoder_1_out5);
  and and_7 (and_7_out, write, decoder_1_out6);
  and and_8 (and_8_out, write, decoder_1_out7);
  _12bit_register u_12bit_register_1 (
    .Input(data), .Reset(reset), .Write(and_1_out), .Clock(clock), .out_5(n12bit_register_1_out_5));
  _12bit_register u_12bit_register_2 (
    .Input(data), .Reset(reset), .Write(and_2_out), .Clock(clock), .out_5(n12bit_register_2_out_5));
  _12bit_register u_12bit_register_3 (
    .Input(data), .Reset(reset), .Write(and_3_out), .Clock(clock), .out_5(n12bit_register_3_out_5));
  _12bit_register u_12bit_register_4 (
    .Input(data), .Reset(reset), .Write(and_4_out), .Clock(clock), .out_5(n12bit_register_4_out_5));
  _12bit_register u_12bit_register_5 (
    .Input(data), .Reset(reset), .Write(and_5_out), .Clock(clock), .out_5(n12bit_register_5_out_5));
  _12bit_register u_12bit_register_6 (
    .Input(data), .Reset(reset), .Write(and_6_out), .Clock(clock), .out_5(n12bit_register_6_out_5));
  _12bit_register u_12bit_register_7 (
    .Input(data), .Reset(reset), .Write(and_7_out), .Clock(clock), .out_5(n12bit_register_7_out_5));
  _12bit_register u_12bit_register_8 (
    .Input(data), .Reset(reset), .Write(and_8_out), .Clock(clock), .out_5(n12bit_register_8_out_5));
  Multiplexer #(.select(3), .width(12), .enable("false")) multiplexer_1 (
    .in0(n12bit_register_1_out_5), .in1(n12bit_register_2_out_5), .in2(n12bit_register_3_out_5),
    .in3(n12bit_register_4_out_5), .in4(n12bit_register_5_out_5), .in5(n12bit_register_6_out_5),
    .in6(n12bit_register_7_out_5), .in7(n12bit_register_8_out_5), .out(S), .sel(rs));
  Multiplexer #(.select(3), .width(12), .enable("false")) multiplexer_2 (
    .in0(n12bit_register_1_out_5), .in1(n12bit_register_2_out_5), .in2(n12bit_register_3_out_5),
    .in3(n12bit_register_4_out_5), .in4(n12bit_register_5_out_5), .in5(n12bit_register_6_out_5),
    .in6(n12bit_register_7_out_5), .in7(n12bit_register_8_out_5), .out(T), .sel(rt));
endmodule

module counter (
  input  Clock,
  input  [11:0] Data,
  output [11:0] Count
);

  wire comparator_1_eq, comparator_1_gt, or_1_out;
  wire [11:0] n12bit_cla_1_p4;

  _12bit_register u_12bit_register_1 (
    .Input(n12bit_cla_1_p4), .Reset(or_1_out), .Write(1'b1), .Clock(Clock), .out_5(Count));
  // _12bit_CLA 12bit_cla_1: pin names not known; wires that end beside it: Count, 12'h1, 1'b0, n12bit_cla_1_p4
  or or_1 (or_1_out, comparator_1_gt, comparator_1_eq);
  Comparator #(.width(12)) comparator_1 (
    .a(n12bit_cla_1_p4), .b(Data), .gt(comparator_1_gt), .eq(comparator_1_eq));  // open: lt
endmodule

module finite_state_machine (
);

  wire clock_1_out, comparator_1_eq, comparator_2_eq, comparator_3_eq, comparator_4_eq, comparator_5_eq,
       comparator_6_eq, comparator_7_eq, decoder_1_out0, decoder_1_out1, decoder_1_out2, decoder_2_out0,
       decoder_2_out1, decoder_2_out2, or_1_out, or_2_out, or_3_out;
  wire [1:0] bitselector_1_out, bitselector_2_out, priority_encoder_1_out, priority_encoder_2_out;
  wire [11:0] bit_extender_1_out, bit_extender_2_out, counter_1_count, n12bit_register_1_out_5,
       n12bit_register_2_out_5;

  Clock clock_1 (.out(clock_1_out));
  counter counter_1 (.Clock(clock_1_out), .Data(12'h1c), .Count(counter_1_count));
  Comparator #(.width(12)) comparator_1 (.a(counter_1_count), .b(12'hd), .eq(comparator_1_eq));  // open: gt, lt
  Comparator #(.width(12)) comparator_2 (.a(counter_1_count), .b(12'h9), .eq(comparator_2_eq));  // open: gt, lt
  Comparator #(.width(12)) comparator_3 (.a(counter_1_count), .b({12{1'b0}}), .eq(comparator_3_eq));  // open: gt, lt
  Comparator #(.width(12)) comparator_4 (.a(counter_1_count), .b(12'h1b), .eq(comparator_4_eq));  // open: gt, lt
  or or_1 (or_1_out, comparator_4_eq, comparator_5_eq);
  Comparator #(.width(12)) comparator_5 (.a(counter_1_count), .b({12{1'b0}}), .eq(comparator_5_eq));  // open: gt, lt
  Comparator #(.width(12)) comparator_6 (.a(counter_1_count), .b(12'h17), .eq(comparator_6_eq));  // open: gt, lt
  Comparator #(.width(12)) comparator_7 (.a(counter_1_count), .b(12'hf), .eq(comparator_7_eq));  // open: gt, lt
  or or_2 (or_2_out, comparator_1_eq, comparator_2_eq, comparator_3_eq);
  Priority_Encoder #(.select(2)) priority_encoder_1 (
    .in0(comparator_1_eq), .in1(comparator_2_eq), .in2(comparator_3_eq), .out(priority_encoder_1_out));  // open: in3, gs, en_out, en_in
  or or_3 (or_3_out, or_1_out, comparator_6_eq, comparator_7_eq);
  Priority_Encoder #(.select(2)) priority_encoder_2 (
    .in0(or_1_out), .in1(comparator_6_eq), .in2(comparator_7_eq), .out(priority_encoder_2_out));  // open: in3, gs, en_out, en_in
  assign bit_extender_1_out = {{10{1'b0}}, priority_encoder_1_out};  // Bit_Extender bit_extender_1
  assign bit_extender_2_out = {{10{1'b0}}, priority_encoder_2_out};  // Bit_Extender bit_extender_2
  _12bit_register u_12bit_register_1 (
    .Input(bit_extender_1_out), .Reset(1'b0), .Write(or_2_out), .Clock(clock_1_out),
    .out_5(n12bit_register_1_out_5));
  _12bit_register u_12bit_register_2 (
    .Input(bit_extender_2_out), .Reset(1'b0), .Write(or_3_out), .Clock(clock_1_out),
    .out_5(n12bit_register_2_out_5));
  BitSelector #(.width(12), .group(2)) bitselector_1 (
    .in(n12bit_register_1_out_5), .out(bitselector_1_out), .sel(3'b000));
  Decoder #(.select(2), .enable("false")) decoder_1 (
    .out0(decoder_1_out0), .out1(decoder_1_out1), .out2(decoder_1_out2), .sel(bitselector_1_out));  // open: out3
  LED led_1 (.in(decoder_1_out0));
  LED led_2 (.in(decoder_1_out1));
  LED led_3 (.in(decoder_1_out2));
  BitSelector #(.width(12), .group(2)) bitselector_2 (
    .in(n12bit_register_2_out_5), .out(bitselector_2_out), .sel(3'b000));
  LED led_4 (.in(decoder_2_out0));
  Decoder #(.select(2), .enable("false")) decoder_2 (
    .out0(decoder_2_out0), .out1(decoder_2_out1), .out2(decoder_2_out2), .sel(bitselector_2_out));  // open: out3
  LED led_5 (.in(decoder_2_out1));
  LED led_6 (.in(decoder_2_out2));

  // Notes on the sheet:
  //   Red
  //   Yellow
  //   Green
  //   Red
  //   Yellow
  //   Green
endmodule

module stack (
  input  Push,
  input  Pop,
  input  [11:0] Data,
  input  C,
  input  reset,
  output Error,
  output [11:0] out_7
);

  wire and_1_out, and_2_out, and_3_out, clock_1_out, comparator_1_eq, not_1_out, not_2_out, or_1_out,
       or_2_out;
  wire [11:0] bit_extender_1_out, multiplexer_1_out, multiplexer_2_out, multiplexer_3_out, n12bit_cla_1_p4,
       n12bit_cla_2_p5, n12bit_register_1_out_5, ram_1_data;

  Clock clock_1 (.out(clock_1_out));
  and and_1 (and_1_out, Pop, ~comparator_1_eq);  // AND_Gate
  or or_1 (or_1_out, and_1_out, Push);
  Multiplexer #(.width(12), .enable("false")) multiplexer_1 (
    .in0(n12bit_cla_2_p5), .in1(n12bit_cla_1_p4), .out(multiplexer_1_out), .sel(Push));
  not not_1 (not_1_out, Push);
  _12bit_register u_12bit_register_1 (
    .Input(multiplexer_1_out), .Reset(1'b0), .Write(or_1_out), .Clock(clock_1_out),
    .out_5(n12bit_register_1_out_5));
  Multiplexer #(.width(12), .enable("false")) multiplexer_2 (
    .in0(n12bit_register_1_out_5), .in1(n12bit_cla_2_p5), .out(multiplexer_2_out), .sel(not_1_out));
  Multiplexer #(.width(12), .enable("false")) multiplexer_3 (
    .in0({12{1'b0}}), .in1(Data), .out(multiplexer_3_out), .sel(Push));
  assign bit_extender_1_out = {{11{1'b0}}, Push};  // Bit_Extender bit_extender_1
  // _12bit_CLA 12bit_cla_1: pin names not known; wires that end beside it: n12bit_register_1_out_5, bit_extender_1_out, 1'b0, n12bit_cla_1_p4
  // _12bit_CLA 12bit_cla_2: pin names not known; wires that end beside it: Data, n12bit_register_1_out_5, {12{1'b1}}, 1'b0, n12bit_cla_2_p5
  not not_2 (not_2_out, clock_1_out);
  Comparator #(.width(12)) comparator_1 (
    .a(n12bit_register_1_out_5), .b({12{1'b0}}), .eq(comparator_1_eq));  // open: gt, lt
  RAM #(.addrWidth(12), .dataWidth(12), .bus("separate")) ram_1 (
    .addr(multiplexer_2_out), .din(multiplexer_3_out), .data(ram_1_data), .str(or_1_out), .clk(not_2_out));  // open: sel, ld, clr
  and and_2 (and_2_out, Pop, comparator_1_eq);
  or or_2 (or_2_out, Push, Pop);
  and and_3 (and_3_out, Push, Pop);
  Multiplexer #(.width(12), .enable("false")) multiplexer_4 (
    .in0(ram_1_data), .in1({12{1'b0}}), .out(out_7), .sel(or_2_out));
  or or_3 (Error, and_3_out, and_2_out);
endmodule
